// Logisim project contadores.circ as structural Verilog
module Contador_Mod16_Asc (
);

  wire clock_1_out, j_k_ff_1_q, j_k_ff_1_qn, j_k_ff_2_q, j_k_ff_2_qn, j_k_ff_3_q, j_k_ff_3_qn, j_k_ff_4_q,
       j_k_ff_4_qn;

  Clock clock_1 (.out(clock_1_out));
  J_K_Flip_Flop j_k_ff_1 (
    .J(1'b1), .K(1'b1), .clk(clock_1_out), .Q(j_k_ff_1_q), .Qn(j_k_ff_1_qn));  // open: preset, reset
  J_K_Flip_Flop j_k_ff_2 (
    .J(1'b1), .K(1'b1), .clk(j_k_ff_1_q), .Q(j_k_ff_2_q), .Qn(j_k_ff_2_qn));  // open: preset, reset
  LED led_1 (.in(j_k_ff_4_qn));
  LED led_2 (.in(j_k_ff_3_qn));
  LED led_3 (.in(j_k_ff_2_qn));
  LED led_4 (.in(j_k_ff_1_qn));
  J_K_Flip_Flop j_k_ff_3 (
    .J(1'b1), .K(1'b1), .clk(j_k_ff_2_q), .Q(j_k_ff_3_q), .Qn(j_k_ff_3_qn));  // open: preset, reset
  J_K_Flip_Flop j_k_ff_4 (
    .J(1'b1), .K(1'b1), .clk(j_k_ff_3_q), .Q(j_k_ff_4_q), .Qn(j_k_ff_4_qn));  // open: preset, reset
endmodule

module Contador_Mod16_Des (
);

  wire clock_1_out, j_k_ff_1_qn, j_k_ff_2_qn, j_k_ff_3_qn, j_k_ff_4_qn;

  Clock clock_1 (.out(clock_1_out));
  J_K_Flip_Flop j_k_ff_1 (.J(1'b1), .K(1'b1), .clk(clock_1_out), .Qn(j_k_ff_1_qn));  // open: Q, preset, reset
  J_K_Flip_Flop j_k_ff_2 (.J(1'b1), .K(1'b1), .clk(j_k_ff_1_qn), .Qn(j_k_ff_2_qn));  // open: Q, preset, reset
  LED led_1 (.in(j_k_ff_4_qn));
  LED led_2 (.in(j_k_ff_3_qn));
  LED led_3 (.in(j_k_ff_2_qn));
  LED led_4 (.in(j_k_ff_1_qn));
  J_K_Flip_Flop j_k_ff_3 (.J(1'b1), .K(1'b1), .clk(j_k_ff_2_qn), .Qn(j_k_ff_3_qn));  // open: Q, preset, reset
  J_K_Flip_Flop j_k_ff_4 (.J(1'b1), .K(1'b1), .clk(j_k_ff_3_qn), .Qn(j_k_ff_4_qn));  // open: Q, preset, reset
endmodule

module Contador_Mod16_AscDes (
  input  in_1
);

  wire clock_1_out, j_k_ff_1_q, j_k_ff_1_qn, j_k_ff_4_qn, n74157_1_pin5, n74157_1_pin6, n74157_1_pin7,
       n74157_1_pin9, n74157_1_pin10, n74157_1_pin11, n74157_1_pin12;

  Clock clock_1 (.out(clock_1_out));
  J_K_Flip_Flop j_k_ff_1 (
    .J(1'b1), .K(1'b1), .clk(clock_1_out), .Q(j_k_ff_1_q), .Qn(j_k_ff_1_qn));  // open: preset, reset
  _74157 u_74157_1 (
    .pin1(in_1), .pin5(n74157_1_pin5), .pin6(n74157_1_pin6), .pin7(n74157_1_pin7), .pin14(j_k_ff_1_q),
    .pin13(j_k_ff_1_qn), .pin12(n74157_1_pin12), .pin11(n74157_1_pin11), .pin10(n74157_1_pin10),
    .pin9(n74157_1_pin9));  // open: pin2, pin3, pin4, pin15
  J_K_Flip_Flop j_k_ff_2 (
    .J(1'b1), .K(1'b1), .clk(n74157_1_pin12), .Q(n74157_1_pin11), .Qn(n74157_1_pin10));  // open: preset, reset
  LED led_1 (.in(j_k_ff_4_qn));
  LED led_2 (.in(n74157_1_pin6));
  LED led_3 (.in(n74157_1_pin10));
  LED led_4 (.in(j_k_ff_1_qn));
  J_K_Flip_Flop j_k_ff_3 (
    .J(1'b1), .K(1'b1), .clk(n74157_1_pin9), .Q(n74157_1_pin5), .Qn(n74157_1_pin6));  // open: preset, reset
  J_K_Flip_Flop j_k_ff_4 (.J(1'b1), .K(1'b1), .clk(n74157_1_pin7), .Qn(j_k_ff_4_qn));  // open: Q, preset, reset
endmodule

module Contador_Mod10_Asc (
);

  wire and_1_out, and_2_out, and_3_out, clock_1_out, j_k_ff_1_q, j_k_ff_1_qn, j_k_ff_2_q, j_k_ff_2_qn,
       j_k_ff_3_q, j_k_ff_3_qn, j_k_ff_4_q, j_k_ff_4_qn, not_1_out, not_2_out;

  Clock clock_1 (.out(clock_1_out));
  and and_1 (and_1_out, and_2_out, not_1_out);
  J_K_Flip_Flop j_k_ff_1 (
    .J(1'b1), .K(1'b1), .clk(clock_1_out), .Q(j_k_ff_1_q), .Qn(j_k_ff_1_qn), .reset(and_1_out));  // open: preset
  and and_2 (and_2_out, and_3_out, not_2_out);
  not not_1 (not_1_out, j_k_ff_2_q);
  and and_3 (and_3_out, j_k_ff_1_q, j_k_ff_3_q);
  J_K_Flip_Flop j_k_ff_2 (
    .J(1'b1), .K(1'b1), .clk(j_k_ff_1_q), .Q(j_k_ff_2_q), .Qn(j_k_ff_2_qn), .reset(and_1_out));  // open: preset
  LED led_1 (.in(j_k_ff_4_qn));
  LED led_2 (.in(j_k_ff_3_qn));
  LED led_3 (.in(j_k_ff_2_qn));
  LED led_4 (.in(j_k_ff_1_qn));
  J_K_Flip_Flop j_k_ff_3 (
    .J(1'b1), .K(1'b1), .clk(j_k_ff_2_q), .Q(j_k_ff_3_q), .Qn(j_k_ff_3_qn), .reset(and_1_out));  // open: preset
  J_K_Flip_Flop j_k_ff_4 (
    .J(1'b1), .K(1'b1), .clk(j_k_ff_3_q), .Q(j_k_ff_4_q), .Qn(j_k_ff_4_qn), .reset(and_1_out));  // open: preset
  not not_2 (not_2_out, j_k_ff_4_q);
endmodule
